# Fritzing sketch card (saved by Fritzing 0.6.2b)
perfboards: 1

parts:
  Arduino1 = Arduino Mega
  J2 = female pin header, 5 pins [form="♂ (male)"]
  J3 = Piezo Speaker

nets:
  N1: Arduino1.D22, J2.pin5
  N2: Arduino1.D24, J2.pin4
  N3: Arduino1.D26, J2.pin3
  N4: Arduino1.D28, J2.pin2
  N5: Arduino1.D30, J2.pin1
  N6: Arduino1.D52, J3.pin2
  N7: Arduino1.GND, J3.pin1

notes:
  verifier la taille de la plaque et la place des connecteur
