# Fritzing sketch mini shield (saved by Fritzing 0.8.7b)
breadboards: 1
perfboards: 1

parts:
  Composant1 = Arduino Mega ADK (Rev3)  # not connected
  Composant2 = Rotoshield - Motor driver shield for Arduino  # not connected
  J1 = RJ11 Jack [package=rj11-6]  # not connected
  U1 = Header 8 [package=1x08_smd]  # not connected
  U2 = Header 8 [package=1x08_smd]
  U4 = Header 6 [package=1x06_smd_straight_alt]
  U5 = Header 6 [package=1x06_smd_straight_alt]
  U7 = 7-SEGMENT-DISPLAY [package=7-segment-display]
  J2 = male pin header, 3 pins [form="♂ (male)"]
  J3 = male pin header, 3 pins [form="♂ (male)"]
  R1 = Resistor [tolerance=±5% resistance=220 package=THT]
  U9 = TMP36 [package=to-92]
  R2 = Resistor [tolerance=±5% resistance=220 package=THT]

nets:
  N1: U2.1, U7.B
  N2: U2.2, U7.DP
  N3: U2.3, U7.D
  N4: U2.4, U7.G1
  N5: U2.7, U9.VOUT
  N6: U2.8, R2.Pin_1
  N7: U4.1, U7.E
  N8: U4.2, U7.G
  N9: U4.4, U7.G2
  N10: U4.5, U7.A
  N11: U4.6, J2.pin3, R1.Pin_1
  N12: U5.3, J3.pin1
  N13: U5.4, J3.pin2
  N14: U5.5, J2.pin1
  N15: U5.6, J2.pin2
  N16: U7.C, R1.Pin_0
